# Fritzing sketch MoreOrLessClock (saved by Fritzing 0.8.7b)
circuit board: 16cm x 20cm
breadboards: 10

parts:
  SR2 = Mystery Part - 16 pins [chip_label=SN74HC595 package=THT]
  Part1 = Arduino Uno (Rev3)
  SR1 = Mystery Part - 16 pins [chip_label=SN74HC595 package=THT]
  SR3 = Mystery Part - 16 pins [chip_label=SN74HC595 package=THT]
  SR4 = Mystery Part - 16 pins [chip_label=SN74HC595 package=THT]
  SSD1 = mystery part, 18 pins [chip_label=7SD]
  RF1 = Resistor [tolerance=±5% resistance=1k package=THT]
  RE1 = Resistor [tolerance=±5% resistance=1k package=THT]
  RD1 = Resistor [tolerance=±5% resistance=1k package=THT]
  RC1 = Resistor [tolerance=±5% resistance=1k package=THT]
  RB1 = Resistor [tolerance=±5% resistance=1k package=THT]
  RA1 = Resistor [tolerance=±5% resistance=1k package=THT]
  RG1 = Resistor [tolerance=±5% resistance=1k package=THT]
  RF2 = Resistor [tolerance=±5% resistance=1k package=THT]
  RC2 = Resistor [tolerance=±5% resistance=1k package=THT]
  RD2 = Resistor [tolerance=±5% resistance=1k package=THT]
  RE2 = Resistor [tolerance=±5% resistance=1k package=THT]
  RA2 = Resistor [tolerance=±5% resistance=1k package=THT]
  RG2 = Resistor [tolerance=±5% resistance=1k package=THT]
  RB2 = Resistor [tolerance=±5% resistance=1k package=THT]
  RF3 = Resistor [tolerance=±5% resistance=1k package=THT]
  RA3 = Resistor [tolerance=±5% resistance=1k package=THT]
  RE3 = Resistor [tolerance=±5% resistance=1k package=THT]
  RG3 = Resistor [tolerance=±5% resistance=1k package=THT]
  RD3 = Resistor [tolerance=±5% resistance=1k package=THT]
  RC3 = Resistor [tolerance=±5% resistance=1k package=THT]
  RB3 = Resistor [tolerance=±5% resistance=1k package=THT]
  RA4 = Resistor [tolerance=±5% resistance=1k package=THT]
  RD4 = Resistor [tolerance=±5% resistance=1k package=THT]
  RB4 = Resistor [tolerance=±5% resistance=1k package=THT]
  RG4 = Resistor [tolerance=±5% resistance=1k package=THT]
  RF4 = Resistor [tolerance=±5% resistance=1k package=THT]
  RC4 = Resistor [tolerance=±5% resistance=1k package=THT]
  RE4 = Resistor [tolerance=±5% resistance=1k package=THT]
  RDP1 = Resistor [tolerance=±5% resistance=1k package=THT]
  RDP2 = Resistor [tolerance=±5% resistance=1k package=THT]
  RDP3 = Resistor [tolerance=±5% resistance=1k package=THT]
  RDP4 = Resistor [tolerance=±5% resistance=1k package=THT]
  SSD2 = mystery part, 18 pins [chip_label=7SD]

nets:
  N1: SR2.pin1, RB2.Pin_0
  N2: SR2.pin2, RC2.Pin_0
  N3: SR2.pin3, RD2.Pin_0
  N4: SR2.pin4, RE2.Pin_0
  N5: SR2.pin5, RF2.Pin_0
  N6: SR2.pin6, RG2.Pin_0
  N7: SR2.pin7, RDP2.Pin_0
  N8: SR2.pin8, SR2.pin13, Part1.GND, SR1.pin8, SR1.pin13, SR3.pin8, SR3.pin13, SR4.pin8, SR4.pin13
  N9: SR2.pin9, SR3.pin14
  N10: SR2.pin10, SR2.pin16, Part1.5V, SR1.pin10, SR1.pin16, SR3.pin10, SR3.pin16, SR4.pin10, SR4.pin16, SSD1.pin13, SSD1.pin14, SSD2.pin13, SSD2.pin14
  N11: SR2.pin11, Part1.D4, SR1.pin11, SR3.pin11, SR4.pin11
  N12: SR2.pin12, Part1.D3_PWM, SR1.pin12, SR3.pin12, SR4.pin12
  N13: SR2.pin14, SR1.pin9
  N14: SR2.pin15, RA2.Pin_0
  N15: Part1.D2, SR1.pin14
  N16: SR1.pin1, RB1.Pin_0
  N17: SR1.pin2, RC1.Pin_0
  N18: SR1.pin3, RD1.Pin_0
  N19: SR1.pin4, RE1.Pin_0
  N20: SR1.pin5, RF1.Pin_0
  N21: SR1.pin6, RG1.Pin_0
  N22: SR1.pin7, RDP1.Pin_0
  N23: SR1.pin15, RA1.Pin_0
  N24: SR3.pin1, RB3.Pin_0
  N25: SR3.pin2, RC3.Pin_0
  N26: SR3.pin3, RD3.Pin_0
  N27: SR3.pin4, RE3.Pin_0
  N28: SR3.pin5, RF3.Pin_0
  N29: SR3.pin6, RG3.Pin_0
  N30: SR3.pin7, RDP3.Pin_0
  N31: SR3.pin9, SR4.pin14
  N32: SR3.pin15, RA3.Pin_0
  N33: SR4.pin1, RB4.Pin_0
  N34: SR4.pin2, RC4.Pin_0
  N35: SR4.pin3, RD4.Pin_0
  N36: SR4.pin4, RE4.Pin_0
  N37: SR4.pin5, RF4.Pin_0
  N38: SR4.pin6, RG4.Pin_0
  N39: SR4.pin7, RDP4.Pin_0
  N40: SR4.pin15, RA4.Pin_0
  N41: SSD1.pin1, RE1.Pin_1
  N42: SSD1.pin2, RD1.Pin_1
  N43: SSD1.pin3, RC1.Pin_1
  N44: SSD1.pin4, RDP1.Pin_1
  N45: SSD1.pin5, RE2.Pin_1
  N46: SSD1.pin6, RD2.Pin_1
  N47: SSD1.pin7, RG2.Pin_1
  N48: SSD1.pin8, RC2.Pin_1
  N49: SSD1.pin9, RDP2.Pin_1
  N50: SSD1.pin10, RB2.Pin_1
  N51: SSD1.pin11, RA2.Pin_1
  N52: SSD1.pin12, RF2.Pin_1
  N53: SSD1.pin15, RB1.Pin_1
  N54: SSD1.pin16, RA1.Pin_1
  N55: SSD1.pin17, RG1.Pin_1
  N56: SSD1.pin18, RF1.Pin_1
  N57: RF3.Pin_1, SSD2.pin18
  N58: RA3.Pin_1, SSD2.pin16
  N59: RE3.Pin_1, SSD2.pin1
  N60: RG3.Pin_1, SSD2.pin17
  N61: RD3.Pin_1, SSD2.pin2
  N62: RC3.Pin_1, SSD2.pin3
  N63: RB3.Pin_1, SSD2.pin15
  N64: RA4.Pin_1, SSD2.pin11
  N65: RD4.Pin_1, SSD2.pin6
  N66: RB4.Pin_1, SSD2.pin10
  N67: RG4.Pin_1, SSD2.pin7
  N68: RF4.Pin_1, SSD2.pin12
  N69: RC4.Pin_1, SSD2.pin8
  N70: RE4.Pin_1, SSD2.pin5
  N71: RDP3.Pin_1, SSD2.pin4
  N72: RDP4.Pin_1, SSD2.pin9

notes:
  Arduino D2 = data pin = SER of SN74HC595
  Arduino D3 = latch pin = RCLK of SN74HC595
  Arduino D4 = clock pin = SRCLK of SN74HC595

custom parts:
  Mystery Part - 16 pins: A dummy, proxy, ersatz, stand-in part for whatever you want. With 16 pins on a 300mil inline pin header footprint.
